// Logisim project CAMINHO_03_Turma_b.circ as structural Verilog: 1 circuit, main circuit main
module main (
  input  in_1,
  input  in_2,
  input  in_3,
  input  in_4,
  input  in_5,
  input  in_6,
  input  [3:0] in_7
);

  wire CLK, registerfile_1_p7;
  wire [4:0] multiplexer_1_out;
  wire [31:0] adder_1_out, bit_extender_1_out, mips_alu_1_p4, mips_ram_1_p6, mipsprogramrom_1_p2,
       multiplexer_2_out, register_1_q, registerfile_1_p1, registerfile_1_p8;

  Clock clock_1 (.out(CLK));
  Adder #(.width(32)) adder_1 (.a(register_1_q), .b(32'h4), .out(adder_1_out));  // open: cin, cout
  Register #(.width(32)) register_1 (.D(adder_1_out), .Q(register_1_q), .clk(CLK));  // open: en, clr
  // MIPSProgramROM mipsprogramrom_1: pin names not known; wires that end beside it: register_1_q, mipsprogramrom_1_p2
  Multiplexer #(.width(5)) multiplexer_1 (
    .in0(mipsprogramrom_1_p2[15:11]), .in1(mipsprogramrom_1_p2[20:16]), .out(multiplexer_1_out), .sel(in_1));  // open: en
  assign bit_extender_1_out = {{16{1'b0}}, mipsprogramrom_1_p2[15:0]};  // Bit_Extender bit_extender_1
  // RegisterFile registerfile_1: pin names not known; wires that end beside it: registerfile_1_p1, CLK, in_2, multiplexer_1_out, mipsprogramrom_1_p2[25:21], mipsprogramrom_1_p2[20:16], registerfile_1_p7, registerfile_1_p8
  Multiplexer #(.width(32)) multiplexer_2 (
    .in0(registerfile_1_p8), .in1(bit_extender_1_out), .out(multiplexer_2_out), .sel(in_3));  // open: en
  // Mips_ALU mips_alu_1: pin names not known; wires that end beside it: registerfile_1_p7, multiplexer_2_out, in_7, mips_alu_1_p4
  // MIPS_RAM mips_ram_1: pin names not known; wires that end beside it: mips_alu_1_p4[19:0], registerfile_1_p8, in_5, CLK, in_4, mips_ram_1_p6
  Multiplexer #(.width(32)) multiplexer_3 (
    .in0(mips_alu_1_p4), .in1(mips_ram_1_p6), .out(registerfile_1_p1), .sel(in_6));  // open: en

  // Other names for the same wires on the sheet: ALU_SRC = in_3; LOAD = in_4; MEM_TO_REG = in_6; REG_DEST = in_1;
  //   REG_W = in_2; STORE = in_5

  // Notes on the sheet:
  //   MEMÓRIA DE PROGRAMA
  //   R
  //   I
  //   VAZIO
endmodule
