// Logisim project aula2.circ as structural Verilog: 1 circuit, main circuit main
module main (
  input  REG_DEST,
  input  MEM_TO_REG,
  input  [3:0] in_3,
  input  ALU_SRC,
  input  \HABILITA_GRAVAÇÃO ,
  output [31:0] DADO_A_SER_GRAVADO
);

  wire clock_1_out, clock_2_out, registerfile_1_p7;
  wire [4:0] mipsprogramrom_1_p2_2, multiplexer_1_out;
  wire [31:0] adder_1_out, bit_extender_1_out, mips_alu_1_p4, mips_ram_1_p1, mipsprogramrom_1_p2,
       multiplexer_2_out, register_1_q, registerfile_1_p8;

  Adder #(.width(32)) adder_1 (.a(register_1_q), .b(32'h4), .out(adder_1_out));  // open: cin, cout
  Register #(.width(32)) register_1 (.D(adder_1_out), .Q(register_1_q), .clk(clock_1_out));  // open: en, clr
  Clock clock_1 (.out(clock_1_out));
  // MIPSProgramROM mipsprogramrom_1: pin names not known; wires that end beside it: register_1_q, {mipsprogramrom_1_p2[31:26], mipsprogramrom_1_p2_2, mipsprogramrom_1_p2[20:0]}
  Multiplexer #(.width(5)) multiplexer_1 (
    .in0(mipsprogramrom_1_p2[15:11]), .in1(mipsprogramrom_1_p2[20:16]), .out(multiplexer_1_out),
    .sel(REG_DEST));  // open: en
  Clock clock_2 (.out(clock_2_out));
  assign bit_extender_1_out = {{16{1'b0}}, mipsprogramrom_1_p2[15:0]};  // Bit_Extender bit_extender_1
  // RegisterFile registerfile_1: pin names not known; wires that end beside it: DADO_A_SER_GRAVADO, clock_2_out, \HABILITA_GRAVAÇÃO , multiplexer_1_out, mipsprogramrom_1_p2[20:16], mipsprogramrom_1_p2_2, registerfile_1_p7, registerfile_1_p8
  Multiplexer #(.width(32)) multiplexer_2 (
    .in0(registerfile_1_p8), .in1(bit_extender_1_out), .out(multiplexer_2_out), .sel(ALU_SRC));  // open: en
  // Mips_ALU mips_alu_1: pin names not known; wires that end beside it: registerfile_1_p7, multiplexer_2_out, in_3, mips_alu_1_p4, mips_alu_1_p4[19:0], registerfile_1_p8
  Multiplexer #(.width(32)) multiplexer_3 (
    .in0(mips_alu_1_p4), .in1(mips_ram_1_p1), .out(DADO_A_SER_GRAVADO), .sel(MEM_TO_REG));  // open: en
  // MIPS_RAM mips_ram_1: pin names not known; wires that end beside it: mips_ram_1_p1

  // Notes on the sheet:
  //   MEMÓRIA DE PROGRAMA
  //   R
  //   I
endmodule
