// Logisim project aula1.circ as structural Verilog: 1 circuit, main circuit main
module main (
  input  [3:0] in_1,
  input  in_2,
  output [5:0] FUNCT,
  output [4:0] SA,
  output [31:0] DADO_A_SER_GRAVADO,
  output [4:0] DESTINO,
  output [4:0] ORIGEM_2,
  output [5:0] OPCODE,
  output [4:0] ORIGEM_1,
  output [4:0] out_10
);

  wire clock_1_out, clock_2_out, registerfile_1_p7, registerfile_1_p8;
  wire [31:0] adder_1_out, register_1_q;

  Adder #(.width(32)) adder_1 (.a(register_1_q), .b(32'h4), .out(adder_1_out));  // open: cin, cout
  Clock clock_1 (.out(clock_1_out));
  Register #(.width(32)) register_1 (.D(adder_1_out), .Q(register_1_q), .clk(clock_1_out));  // open: en, clr
  // MIPSProgramROM mipsprogramrom_1: pin names not known; wires that end beside it: register_1_q, {OPCODE, ORIGEM_1, ORIGEM_2, DESTINO, SA, FUNCT}
  Clock clock_2 (.out(clock_2_out));
  // RegisterFile registerfile_1: pin names not known; wires that end beside it: DADO_A_SER_GRAVADO, clock_2_out, in_2, DESTINO, ORIGEM_1, ORIGEM_2, registerfile_1_p7, registerfile_1_p8
  // Mips_ALU mips_alu_1: pin names not known; wires that end beside it: registerfile_1_p7, registerfile_1_p8, in_1, DADO_A_SER_GRAVADO

  assign out_10 = DESTINO;

  // Notes on the sheet:
  //   MEMÓRIA DE PROGRAMA
endmodule
