// Logisim project aula4.circ as structural Verilog: 1 circuit, main circuit main
module main (
  input  [3:0] in_1,
  output ADDIU,
  output SW,
  output LW
);

  wire ALU_SRC, CLK, REG_DEST, REG_W, registerfile_1_p7;
  wire [4:0] multiplexer_1_out;
  wire [31:0] adder_1_out, bit_extender_1_out, mips_alu_1_p4, mips_ram_1_p6, mipsprogramrom_1_p2,
       multiplexer_2_out, register_1_q, registerfile_1_p1, registerfile_1_p8;

  Adder #(.width(32)) adder_1 (.a(register_1_q), .b(32'h4), .out(adder_1_out));  // open: cin, cout
  Register #(.width(32)) register_1 (.D(adder_1_out), .Q(register_1_q), .clk(CLK));  // open: en, clr
  // MIPSProgramROM mipsprogramrom_1: pin names not known; wires that end beside it: register_1_q, mipsprogramrom_1_p2
  Multiplexer #(.width(5)) multiplexer_1 (
    .in0(mipsprogramrom_1_p2[15:11]), .in1(mipsprogramrom_1_p2[20:16]), .out(multiplexer_1_out),
    .sel(REG_DEST));  // open: en
  and and_1 (ADDIU, mipsprogramrom_1_p2[26], ~mipsprogramrom_1_p2[27], ~mipsprogramrom_1_p2[28], mipsprogramrom_1_p2[29], ~mipsprogramrom_1_p2[30], ~mipsprogramrom_1_p2[31]);  // AND_Gate
  and and_2 (SW, mipsprogramrom_1_p2[26], mipsprogramrom_1_p2[27], ~mipsprogramrom_1_p2[28], mipsprogramrom_1_p2[29], ~mipsprogramrom_1_p2[30], mipsprogramrom_1_p2[31]);  // AND_Gate
  and and_3 (LW, mipsprogramrom_1_p2[26], mipsprogramrom_1_p2[27], ~mipsprogramrom_1_p2[28], ~mipsprogramrom_1_p2[29], ~mipsprogramrom_1_p2[30], mipsprogramrom_1_p2[31]);  // AND_Gate
  assign bit_extender_1_out = {{16{1'b0}}, mipsprogramrom_1_p2[15:0]};  // Bit_Extender bit_extender_1
  Clock clock_1 (.out(CLK));
  or or_1 (REG_DEST, ADDIU, LW, SW);
  or or_2 (REG_W, ADDIU, LW);
  or or_3 (ALU_SRC, ADDIU, LW, SW);
  // RegisterFile registerfile_1: pin names not known; wires that end beside it: registerfile_1_p1, CLK, REG_W, multiplexer_1_out, mipsprogramrom_1_p2[25:21], mipsprogramrom_1_p2[20:16], registerfile_1_p7, registerfile_1_p8
  Multiplexer #(.width(32)) multiplexer_2 (
    .in0(registerfile_1_p8), .in1(bit_extender_1_out), .out(multiplexer_2_out), .sel(ALU_SRC));  // open: en
  // Mips_ALU mips_alu_1: pin names not known; wires that end beside it: registerfile_1_p7, multiplexer_2_out, in_1, mips_alu_1_p4
  // MIPS_RAM mips_ram_1: pin names not known; wires that end beside it: mips_alu_1_p4[19:0], registerfile_1_p8, SW, CLK, LW, mips_ram_1_p6
  Multiplexer #(.width(32)) multiplexer_3 (
    .in0(mips_alu_1_p4), .in1(mips_ram_1_p6), .out(registerfile_1_p1), .sel(LW));  // open: en

  // Other names for the same wires on the sheet: LOAD = LW; MEM_TO_REG = LW; STORE = SW

  // Notes on the sheet:
  //   MEMÓRIA DE PROGRAMA
  //   OPCODE
  //   R
  //   I
  //   VAZIO
  //   0 = R e 1 = I
  //   0 = R e 1 = I
  //   VAZIO
endmodule
