// Logisim project Projeto.circ as structural Verilog: 3 circuits, main circuit ULA
module ULA (
  input  [7:0] in_1,
  input  [2:0] in_2,
  input  [7:0] in_3,
  input  [2:0] in_4,
  input  [3:0] in_5,
  output [7:0] out_6
);

  wire [7:0] and_1_out, nor_1_out, or_1_out, shifter_1_out, shifter_2_out, somador8bits_1_out_3,
       subtrator8bits_1_out_3, xor_1_out;

  assign and_1_out = in_1 & in_3;  // AND_Gate and_1, 8 bits wide
  assign xor_1_out = in_1 ^ in_3;  // XOR_Gate xor_1, 8 bits wide
  assign or_1_out = in_1 | in_3;  // OR_Gate or_1, 8 bits wide
  assign nor_1_out = ~(in_1 | in_3);  // NOR_Gate nor_1, 8 bits wide
  Shifter shifter_1 (.in(in_1), .\dist (in_2), .out(shifter_1_out));
  Somador8Bits somador8bits_1 (.out_3(somador8bits_1_out_3), .in_2(in_3), .in_1(in_1));
  Shifter #(.shift("lr")) shifter_2 (.in(in_1), .\dist (in_4), .out(shifter_2_out));
  Subtrator8Bits subtrator8bits_1 (.out_3(subtrator8bits_1_out_3), .in_2(in_3), .in_1(in_1));
  Multiplexer #(.select(4), .width(8), .enable("false")) multiplexer_1 (
    .in0(shifter_1_out), .in1(and_1_out), .in5(subtrator8bits_1_out_3), .in6(shifter_2_out),
    .in8(somador8bits_1_out_3), .in10(nor_1_out), .in12(or_1_out), .in15(xor_1_out), .out(out_6), .sel(in_5));  // open: in2, in3, in4, in7, in9, in11, in13, in14

  // Notes on the sheet:
  //   A
  //   B
  //   S
endmodule

module Somador8Bits (
  input  [7:0] in_1,
  input  [7:0] in_2,
  output [7:0] out_3
);

  wire somadorcompleto_2_out_5, somadorcompleto_3_out_5, somadorcompleto_4_out_5, somadorcompleto_5_out_5,
       somadorcompleto_6_out_5, somadorcompleto_7_out_5, somadorcompleto_8_out_5;

  SomadorCompleto somadorcompleto_1 (
    .out_4(out_3[7]), .in_2(in_2[7]), .in_1(in_1[7]), .in_3(somadorcompleto_2_out_5));  // open: out_5
  SomadorCompleto somadorcompleto_2 (
    .out_4(out_3[6]), .in_2(in_2[6]), .in_1(in_1[6]), .in_3(somadorcompleto_3_out_5),
    .out_5(somadorcompleto_2_out_5));
  SomadorCompleto somadorcompleto_3 (
    .out_4(out_3[5]), .in_2(in_2[5]), .in_1(in_1[5]), .in_3(somadorcompleto_4_out_5),
    .out_5(somadorcompleto_3_out_5));
  SomadorCompleto somadorcompleto_4 (
    .out_4(out_3[4]), .in_2(in_2[4]), .in_1(in_1[4]), .in_3(somadorcompleto_5_out_5),
    .out_5(somadorcompleto_4_out_5));
  SomadorCompleto somadorcompleto_5 (
    .out_4(out_3[3]), .in_2(in_2[3]), .in_1(in_1[3]), .in_3(somadorcompleto_6_out_5),
    .out_5(somadorcompleto_5_out_5));
  SomadorCompleto somadorcompleto_6 (
    .out_4(out_3[2]), .in_2(in_2[2]), .in_1(in_1[2]), .in_3(somadorcompleto_7_out_5),
    .out_5(somadorcompleto_6_out_5));
  SomadorCompleto somadorcompleto_7 (
    .out_4(out_3[1]), .in_2(in_2[1]), .in_1(in_1[1]), .in_3(somadorcompleto_8_out_5),
    .out_5(somadorcompleto_7_out_5));
  SomadorCompleto somadorcompleto_8 (
    .out_4(out_3[0]), .in_2(in_2[0]), .in_1(in_1[0]), .in_3(1'b0), .out_5(somadorcompleto_8_out_5));

  // Notes on the sheet:
  //   A
  //   B
  //   S
endmodule

module Subtrator8Bits (
  input  [7:0] in_1,
  input  [7:0] in_2,
  output [7:0] out_3
);

  wire subtratorcompleto_2_bout, subtratorcompleto_3_bout, subtratorcompleto_4_bout,
       subtratorcompleto_5_bout, subtratorcompleto_6_bout, subtratorcompleto_7_bout, subtratorcompleto_8_bout;

  SubtratorCompleto subtratorcompleto_1 (
    .S(out_3[7]), .B(in_1[7]), .A(in_2[7]), .Bin(subtratorcompleto_2_bout));  // open: Bout
  SubtratorCompleto subtratorcompleto_2 (
    .S(out_3[6]), .B(in_1[6]), .A(in_2[6]), .Bin(subtratorcompleto_3_bout), .Bout(subtratorcompleto_2_bout));
  SubtratorCompleto subtratorcompleto_3 (
    .S(out_3[5]), .B(in_1[5]), .A(in_2[5]), .Bin(subtratorcompleto_4_bout), .Bout(subtratorcompleto_3_bout));
  SubtratorCompleto subtratorcompleto_4 (
    .S(out_3[4]), .B(in_1[4]), .A(in_2[4]), .Bin(subtratorcompleto_5_bout), .Bout(subtratorcompleto_4_bout));
  SubtratorCompleto subtratorcompleto_5 (
    .S(out_3[3]), .B(in_1[3]), .A(in_2[3]), .Bin(subtratorcompleto_6_bout), .Bout(subtratorcompleto_5_bout));
  SubtratorCompleto subtratorcompleto_6 (
    .S(out_3[2]), .B(in_1[2]), .A(in_2[2]), .Bin(subtratorcompleto_7_bout), .Bout(subtratorcompleto_6_bout));
  SubtratorCompleto subtratorcompleto_7 (
    .S(out_3[1]), .B(in_1[1]), .A(in_2[1]), .Bin(subtratorcompleto_8_bout), .Bout(subtratorcompleto_7_bout));
  SubtratorCompleto subtratorcompleto_8 (
    .S(out_3[0]), .B(in_1[0]), .A(in_2[0]), .Bin(1'b0), .Bout(subtratorcompleto_8_bout));
endmodule
