// Logisim project Relatorio1.circ as structural Verilog: 4 circuits, main circuit MeioSomador
module MeioSomador (
  input  A,
  input  B,
  output S,
  output Cout
);

  xor xor_1 (S, A, B);
  and and_1 (Cout, A, B);
endmodule

module SomadorCompleto (
  input  in_1,
  input  in_2,
  input  in_3,
  output out_4,
  output out_5
);

  wire meiosomador_1_cout, meiosomador_1_s, meiosomador_2_cout;

  MeioSomador meiosomador_1 (.Cout(meiosomador_1_cout), .B(in_2), .A(in_1), .S(meiosomador_1_s));
  MeioSomador meiosomador_2 (.Cout(meiosomador_2_cout), .B(in_3), .A(meiosomador_1_s), .S(out_4));
  or or_1 (out_5, meiosomador_2_cout, meiosomador_1_cout);
endmodule

module MeioSubtrator (
  input  A,
  input  B,
  output S,
  output Bout
);

  wire not_1_out;

  not not_1 (not_1_out, A);
  xor xor_1 (S, A, B);
  and and_1 (Bout, B, not_1_out);
endmodule

module SubtratorCompleto (
  input  A,
  input  B,
  input  Bin,
  output S,
  output Bout
);

  wire meiosubtrator_1_bout, meiosubtrator_1_s, meiosubtrator_2_bout;

  MeioSubtrator meiosubtrator_1 (.Bout(meiosubtrator_1_bout), .B(B), .A(A), .S(meiosubtrator_1_s));
  MeioSubtrator meiosubtrator_2 (.Bout(meiosubtrator_2_bout), .B(Bin), .A(meiosubtrator_1_s), .S(S));
  or or_1 (Bout, meiosubtrator_1_bout, meiosubtrator_2_bout);
endmodule
