// Logisim project Relatorio2Certo.circ as structural Verilog: 3 circuits, main circuit Multiplicacao
module Multiplicacao (
  input  A1,
  input  A0,
  input  B1,
  input  B0,
  output P3,
  output P2,
  output P1,
  output P0
);

  wire and_1_out, and_2_out, and_3_out, meiosomador_2_cout;

  and and_1 (and_1_out, A1, B1);
  and and_2 (and_2_out, A1, B0);
  and and_3 (and_3_out, A0, B1);
  and and_4 (P0, A0, B0);
  MeioSomador meiosomador_1 (.Cout(P3), .B(and_1_out), .A(meiosomador_2_cout), .S(P2));
  MeioSomador meiosomador_2 (.Cout(meiosomador_2_cout), .B(and_2_out), .A(and_3_out), .S(P1));
endmodule

module Complemento2 (
  input  [3:0] A,
  input  [3:0] B,
  input  CIN,
  output [3:0] S,
  output COUT
);

  wire multiplexer_1_out, multiplexer_2_out, multiplexer_3_out, multiplexer_4_out, not_1_out, not_2_out,
       not_4_out, not_5_out, somadorcompleto_1_out_5, somadorcompleto_2_out_5, somadorcompleto_3_out_5;

  not not_1 (not_1_out, B[0]);
  not not_2 (not_2_out, B[1]);
  not not_3 (not_2_out, B[1]);
  not not_4 (not_4_out, B[2]);
  not not_5 (not_5_out, B[3]);
  Multiplexer #(.enable("false")) multiplexer_1 (.in0(B[0]), .in1(not_1_out), .out(multiplexer_1_out), .sel(CIN));
  Multiplexer #(.enable("false")) multiplexer_2 (.in0(B[1]), .in1(not_2_out), .out(multiplexer_2_out), .sel(CIN));
  Multiplexer #(.enable("false")) multiplexer_3 (.in0(B[2]), .in1(not_4_out), .out(multiplexer_3_out), .sel(CIN));
  Multiplexer #(.enable("false")) multiplexer_4 (.in0(B[3]), .in1(not_5_out), .out(multiplexer_4_out), .sel(CIN));
  SomadorCompleto somadorcompleto_1 (
    .out_4(S[0]), .in_2(multiplexer_1_out), .in_1(A[0]), .in_3(CIN), .out_5(somadorcompleto_1_out_5));
  SomadorCompleto somadorcompleto_2 (
    .out_4(S[1]), .in_2(multiplexer_2_out), .in_1(A[1]), .in_3(somadorcompleto_1_out_5),
    .out_5(somadorcompleto_2_out_5));
  SomadorCompleto somadorcompleto_3 (
    .out_4(S[2]), .in_2(multiplexer_3_out), .in_1(A[2]), .in_3(somadorcompleto_2_out_5),
    .out_5(somadorcompleto_3_out_5));
  SomadorCompleto somadorcompleto_4 (
    .out_4(S[3]), .in_2(multiplexer_4_out), .in_1(A[3]), .in_3(somadorcompleto_3_out_5), .out_5(COUT));
endmodule

module RegistradorDeslocamento (
  input  [3:0] D,
  input  Clock,
  input  Carga,
  input  Clear,
  output [3:0] Q
);

  wire multiplexer_1_out, multiplexer_2_out, multiplexer_3_out, multiplexer_4_out;

  D_Flip_Flop d_ff_1 (.D(multiplexer_1_out), .clk(Clock), .Q(Q[0]), .reset(Clear));  // open: Qn, preset
  Multiplexer #(.enable("false")) multiplexer_1 (.in0(Q[0]), .in1(D[0]), .out(multiplexer_1_out), .sel(Carga));
  Multiplexer #(.enable("false")) multiplexer_2 (.in0(Q[1]), .in1(D[1]), .out(multiplexer_2_out), .sel(Carga));
  D_Flip_Flop d_ff_2 (.D(multiplexer_2_out), .clk(Clock), .Q(Q[1]), .reset(Clear));  // open: Qn, preset
  Multiplexer #(.enable("false")) multiplexer_3 (.in0(Q[2]), .in1(D[2]), .out(multiplexer_3_out), .sel(Carga));
  D_Flip_Flop d_ff_3 (.D(multiplexer_3_out), .clk(Clock), .Q(Q[2]), .reset(Clear));  // open: Qn, preset
  Multiplexer #(.enable("false")) multiplexer_4 (.in0(Q[3]), .in1(D[3]), .out(multiplexer_4_out), .sel(Carga));
  D_Flip_Flop d_ff_4 (.D(multiplexer_4_out), .clk(Clock), .Q(Q[3]), .reset(Clear));  // open: Qn, preset
endmodule
