// Logisim project Relatorio1Exercicio.circ as structural Verilog: 2 circuits, main circuit Exercicio1
module Exercicio1 (
  input  [2:0] in_1,
  input  in_2,
  output [1:0] out_3
);

  wire [1:0] somadorcompleto_1_out_4, subtratorcompleto_1_s;
  wire [2:0] demultiplexer_1_out0, demultiplexer_1_out1;

  Demultiplexer #(.width(3), .enable("false")) demultiplexer_1 (
    .out0(demultiplexer_1_out0), .out1(demultiplexer_1_out1), .in(in_1), .sel(in_2));
  SomadorCompleto somadorcompleto_1 (
    .out_4(somadorcompleto_1_out_4[0]), .in_2(demultiplexer_1_out0[1]), .in_1(demultiplexer_1_out0[0]),
    .in_3(demultiplexer_1_out0[2]), .out_5(somadorcompleto_1_out_4[1]));
  SubtratorCompleto subtratorcompleto_1 (
    .S(subtratorcompleto_1_s[0]), .B(demultiplexer_1_out1[1]), .A(demultiplexer_1_out1[0]),
    .Bin(demultiplexer_1_out1[2]), .Bout(subtratorcompleto_1_s[1]));
  Multiplexer #(.width(2), .enable("false")) multiplexer_1 (
    .in0(somadorcompleto_1_out_4), .in1(subtratorcompleto_1_s), .out(out_3), .sel(in_2));

  // Notes on the sheet:
  //   USANDO SUBTRATOR E SOMADOR COMPLETO
endmodule

module Exercicio2 (
  input  [1:0] in_1,
  input  in_2,
  output [1:0] out_3
);

  wire [1:0] demultiplexer_1_out0, demultiplexer_1_out1, meiosomador_1_s, meiosubtrator_1_s;

  Demultiplexer #(.width(2), .enable("false")) demultiplexer_1 (
    .out0(demultiplexer_1_out0), .out1(demultiplexer_1_out1), .in(in_1), .sel(in_2));
  MeioSomador meiosomador_1 (
    .Cout(meiosomador_1_s[1]), .B(demultiplexer_1_out0[1]), .A(demultiplexer_1_out0[0]),
    .S(meiosomador_1_s[0]));
  MeioSubtrator meiosubtrator_1 (
    .Bout(meiosubtrator_1_s[1]), .B(demultiplexer_1_out1[1]), .A(demultiplexer_1_out1[0]),
    .S(meiosubtrator_1_s[0]));
  Multiplexer #(.width(2), .enable("false")) multiplexer_1 (
    .in0(meiosomador_1_s), .in1(meiosubtrator_1_s), .out(out_3), .sel(in_2));

  // Notes on the sheet:
  //   USANDO MEIO SOMADOR E MEIO SUTRATOR
endmodule
